# Fritzing sketch NFC_RTC (saved by Fritzing 0.9.3b)
breadboards: 1

parts:
  Part1 = Arduino Uno (Rev3)
  PN532_-_NFC = Arduino Prototyping Shield
  DS3231SN = Real Time Clock Module - DS1307 RTC Breakout Board

nets:
  GND: Part1.GND, PN532_-_NFC.GND, DS3231SN.GND
  N1: Part1.A4/SDA, PN532_-_NFC.SDA, DS3231SN.SDA
  N2: Part1.A5/SCL, PN532_-_NFC.SCL, DS3231SN.SCL
  N3: Part1.D2, PN532_-_NFC.D2
  5V: Part1.5V, PN532_-_NFC.+5V, DS3231SN.5V

notes:
  IRQ
